# Fritzing sketch power_metering_breadboard (saved by Fritzing 0.9.2b)
circuit board: 8.46667cm x 5.64444cm
breadboards: 1

parts:
  R3 = Resistor [tolerance=±5% resistance=10k package=THT]
  U1 = TLP621 [part_number="Get Impulse from Wattmeter" package=THT]
  Part1 = Arduino Yun
  U2 = TLP621 [part_number="Get Impulse from Wattmeter" package=THT]
  R4 = Resistor [tolerance=±5% resistance=10k package=THT]

nets:
  N1: R3.Pin_0, Part1.5V, R4.Pin_1
  N2: R3.Pin_1, U1.Pin_4, Part1.D2/SDA, Part1.D2
  N3: U1.Pin_3, Part1.GND, U2.Pin_3
  N4: Part1.D3/SCL, Part1.D3_PWM, U2.Pin_4, R4.Pin_0
