# Fritzing sketch power_metering_protoshield (saved by Fritzing 0.9.2b)

parts:
  R2 = Resistor [tolerance=±5% resistance=10k package=THT]
  U2 = TLP621 [part_number="Get Impulse from Wattmeter \"Two\"" package=THT]
  Part1 = Arduino Yun  # not connected
  Part2 = Arduino Prototyping Shield
  R3 = Resistor [tolerance=±5% resistance=10k package=THT]
  U3 = TLP621 [part_number="Get Impulse from Wattmeter \"One\"" package=THT]

nets:
  N1: R2.Pin_0, Part2.+5V, Part2.N$241, Part2.N$376, R3.Pin_0
  N2: R2.Pin_1, U2.Pin_4, Part2.D2, Part2.N$81
  N3: U2.Pin_3, Part2.GND, U3.Pin_3
  N4: Part2.D3, Part2.N$165, R3.Pin_1, U3.Pin_4
